# Fritzing sketch postbox-monitor-diagram (saved by Fritzing 0.9.3b)

parts:
  Part2 = Arduino Nano (Rev3.0)
  Part3 = KY-021 Mini Magnetic Reed Switch Module [package="Breakout board"]
  Part4 = KY-021 Mini Magnetic Reed Switch Module [package="Breakout board"]
  Part5 = Bluetooth HC-05 Macho
  BAT1 = BC9VPC [package=bc9vpc]

nets:
  N1: Part2.D1/TX, Part5.TXD
  N2: Part2.D0/RX, Part5.RXD
  GND: Part2.GND, Part3.-, Part4.-, Part5.GND, BAT1.V-
  N3: Part2.D2, Part4.S
  N4: Part2.D3, Part3.S
  N5: Part2.VIN, BAT1.V+
  VIN: Part2.5V, Part3.Vin, Part4.Vin, Part5.VCC
  N6: Part2.A1, Part5.State
  N7: Part2.A0, Part5.Key

custom parts:
  KY-021 Mini Magnetic Reed Switch Module: KY-021 magnetic reed switch module. A reed switch is a magnetic sensor that is normally open and gets closed when exposed to a magnetic field.
